# Fritzing sketch IO Bus (saved by Fritzing 0.8.7b)
breadboards: 3

parts:
  INPUT-I0 = male pin header, 6 pins [form="♂ (male)"]
  INPUT-I1 = male pin header, 6 pins [form="♂ (male)"]
  OUTPUT-O0 = male pin header, 6 pins [form="♂ (male)"]
  OUTPUT-O1 = male pin header, 6 pins [form="♂ (male)"]
  74HC125 = IC, DIP package, 14 pins [chip_label=74HC125]
  IC1 = IC, DIP package, 16 pins [chip_label=74LS138]
  IC2 = IC, DIP package, 16 pins [chip_label=74LS138]
  INPUT-I2 = male pin header, 6 pins [form="♂ (male)"]
  OUTPUT-O2 = male pin header, 6 pins [form="♂ (male)"]
  OUTPUT-O3 = male pin header, 6 pins [form="♂ (male)"]
  R1 = Resistor [tolerance=±5% resistance=10k package=THT]
  INPUT-I3 = male pin header, 6 pins [form="♂ (male)"]
  R2 = Resistor [tolerance=±5% resistance=1k package=THT]
  74HC126 = IC, DIP package, 14 pins [chip_label=74HC125]
  J5 = male pin header, 11 pins [form="♂ (male)"]
  R3 = Resistor [tolerance=±5% resistance=4.7k package=THT]
  R4 = Resistor [tolerance=±5% resistance=4.7k package=THT]

nets:
  N1: INPUT-I0.pin1, INPUT-I1.pin1, OUTPUT-O0.pin1, OUTPUT-O1.pin1, 74HC125.pin14, IC1.pin6, IC1.pin16, IC2.pin16, R1.Pin_1, 74HC126.pin14, J5.pin6
  N2: INPUT-I0.pin2, INPUT-I0.pin4, INPUT-I1.pin2, INPUT-I1.pin4, OUTPUT-O0.pin2, OUTPUT-O1.pin2, 74HC125.pin7, IC1.pin8, IC2.pin5, IC2.pin8, R2.Pin_0, 74HC126.pin7, J5.pin7, R3.Pin_1, R4.Pin_1
  N3: INPUT-I0.pin3, 74HC125.pin2, R3.Pin_0
  N4: INPUT-I0.pin5, INPUT-I1.pin5, OUTPUT-O0.pin5, OUTPUT-O1.pin5, INPUT-I2.pin5, OUTPUT-O2.pin5, OUTPUT-O3.pin5, INPUT-I3.pin5, J5.pin10
  N5: INPUT-I0.pin6, INPUT-I1.pin6, INPUT-I2.pin6, INPUT-I3.pin6, J5.pin11
  N6: INPUT-I1.pin3, 74HC125.pin5, R4.Pin_0
  N7: OUTPUT-O0.pin3, OUTPUT-O1.pin3, OUTPUT-O2.pin3, OUTPUT-O3.pin3, J5.pin9
  N8: OUTPUT-O0.pin4, 74HC125.pin1, IC1.pin15
  N9: OUTPUT-O1.pin4, 74HC125.pin4, IC1.pin14
  N10: 74HC125.pin3, 74HC125.pin6, 74HC125.pin8, 74HC125.pin11, R2.Pin_1, 74HC126.pin3, 74HC126.pin6, 74HC126.pin8, 74HC126.pin11, J5.pin8
  N11: 74HC125.pin9, INPUT-I3.pin3
  N12: 74HC125.pin10, IC1.pin13, OUTPUT-O2.pin4
  N13: 74HC125.pin12, INPUT-I2.pin3
  N14: 74HC125.pin13, IC1.pin12, OUTPUT-O3.pin4
  N15: IC1.pin1, IC2.pin1, J5.pin1
  N16: IC1.pin2, IC2.pin2, J5.pin2
  N17: IC1.pin3, IC2.pin3, J5.pin3
  N18: IC1.pin4, IC2.pin4, R1.Pin_0, J5.pin5
  N19: IC1.pin5, IC2.pin6, J5.pin4
  N20: IC1.pin7, 74HC126.pin13
  N21: IC1.pin9, 74HC126.pin10
  N22: IC1.pin10, 74HC126.pin4
  N23: IC1.pin11, 74HC126.pin1

notes:
  A0
  A1
  A2
  ADDR_EN
  VCC
  GND
  MISO
  MOSI
  CLK
  IN_LATCH
  LOAD
  EN
  N/C
  OUTPUTS
  INPUTS
  A3
