# Fritzing sketch Input Module (saved by Fritzing 0.8.7b)
circuit board: 2.55349cm x 4.0889cm
perfboards: 1

parts:
  R3 = Resistor [tolerance=±5% resistance=4.7k package=THT]
  R7 = Resistor [tolerance=±5% resistance=4.7k package=THT]
  R2 = Resistor [tolerance=±5% resistance=4.7k package=THT]
  IC1 = IC, DIP package, 16 pins [chip_label=74LS165]
  J1 = double row male pin header, 16 pins [form="♂ (male)"]
  R8 = Resistor [tolerance=±5% resistance=4.7k package=THT]
  R1 = Resistor [tolerance=±5% resistance=4.7k package=THT]
  R9 = Resistor [tolerance=±5% resistance=4.7k package=THT]
  R6 = Resistor [tolerance=±5% resistance=4.7k package=THT]
  J2 = male pin header, 6 pins [form="♂ (male)"]
  R4 = Resistor [tolerance=±5% resistance=4.7k package=THT]

nets:
  N1: R3.Pin_0, IC1.pin12, J1.pin15
  N2: R3.Pin_1, R7.Pin_1, R2.Pin_1, IC1.pin8, R8.Pin_1, R1.Pin_1, R9.Pin_1, R6.Pin_1, J2.pin2, R4.Pin_1
  N3: R7.Pin_0, IC1.pin3, J1.pin12
  N4: R2.Pin_0, IC1.pin13, J1.pin14
  N5: IC1.pin1, J2.pin6
  N6: IC1.pin2, J2.pin5
  N7: IC1.pin4, J1.pin11, R8.Pin_0
  N8: IC1.pin5, J1.pin10, R6.Pin_0
  N9: IC1.pin6, J1.pin9, R9.Pin_0
  N10: IC1.pin9, J2.pin3
  N11: IC1.pin11, J1.pin16, R4.Pin_0
  N12: IC1.pin14, J1.pin13, R1.Pin_0
  N13: IC1.pin15, J2.pin4
  N14: IC1.pin16, J1.pin1, J1.pin2, J1.pin3, J1.pin4, J1.pin5, J1.pin6, J1.pin7, J1.pin8, J2.pin1

notes:
  VCC
  EN
  CLK
  MISO
  GND
  LOAD
