# Fritzing sketch Output Module (saved by Fritzing 0.8.7b)
circuit board: 2.5481cm x 4.0579cm
breadboards: 1

parts:
  J4 = male pin header, 6 pins [form="♂ (male)"]
  R14 = Resistor [tolerance=±5% resistance=330 package=THT]
  R15 = Resistor [tolerance=±5% resistance=330 package=THT]
  R16 = Resistor [tolerance=±5% resistance=330 package=THT]
  R17 = Resistor [tolerance=±5% resistance=330 package=THT]
  U1 = 74HC595 [package="DIP16 [THT]"]
  R18 = Resistor [tolerance=±5% resistance=330 package=THT]
  R19 = Resistor [tolerance=±5% resistance=330 package=THT]
  R20 = Resistor [tolerance=±5% resistance=330 package=THT]
  R21 = Resistor [tolerance=±5% resistance=330 package=THT]
  J5 = double row male pin header, 16 pins [form="♂ (male)"]

nets:
  N1: J4.pin1, U1.MR, U1.VCC, J5.pin1, J5.pin2, J5.pin3, J5.pin4, J5.pin5, J5.pin6, J5.pin7, J5.pin8
  N2: J4.pin2, U1.GND, U1.OE
  N3: J4.pin3, U1.DS
  N4: J4.pin4, U1.ST_CP
  N5: J4.pin5, U1.SH_CP
  N6: R14.Pin_0, U1.Q7
  N7: R14.Pin_1, J5.pin9
  N8: R15.Pin_0, U1.Q6
  N9: R15.Pin_1, J5.pin10
  N10: R16.Pin_0, U1.Q5
  N11: R16.Pin_1, J5.pin11
  N12: R17.Pin_0, U1.Q4
  N13: R17.Pin_1, J5.pin12
  N14: U1.Q1, R20.Pin_0
  N15: U1.Q2, R19.Pin_0
  N16: U1.Q3, R18.Pin_0
  N17: U1.Q0, R21.Pin_0
  N18: R18.Pin_1, J5.pin13
  N19: R19.Pin_1, J5.pin14
  N20: R20.Pin_1, J5.pin15
  N21: R21.Pin_1, J5.pin16
